# Fritzing sketch DrectWay (saved by Fritzing 0.8.7b)
breadboards: 1

parts:
  Part1 = Arduino Uno (Rev3)
  M1 = DC Motor
  S1 = H-Bridge with L298N
  M2 = DC Motor
  VCC1 = Battery block 9V
  Part2 = SRF05 Ultrasonic Rangefinder
  M3 = fc-51 [package=THT]
  M4 = fc-51 [package=THT]
  M5 = fc-51 [package=THT]
  M6 = fc-51 [package=THT]
  J1 = Basic Servo

nets:
  N1: Part1.A2, M6.pin1
  N2: Part1.A3, M5.pin1
  N3: Part1.A4/SDA, M4.pin1
  N4: Part1.A5/SCL, M3.pin1
  N5: Part1.D8, Part2.Trig
  N6: Part1.D10_PWM/SS, S1.IN2
  N7: Part1.D11_PWM/MOSI, S1.IN1
  N8: Part1.D12/MISO, S1.ENB
  N9: Part1.D13/SCK, S1.ENA
  N10: Part1.D5_PWM, S1.IN4
  N11: Part1.D6_PWM, S1.IN3
  N12: Part1.D7, Part2.Echo
  GND: Part1.GND, S1.GND, VCC1.-
  VIN: Part1.VIN, S1.12V, VCC1.+
  N13: M1.pin_1, S1.M2-02
  N14: M1.pin_2, S1.M2-01
  N15: S1.M1-01, M2.pin_2
  N16: S1.M1-02, M2.pin_1
  VCC: Part2.VCC, M3.pin3, M4.pin3, M5.pin3, M6.pin3, J1.vcc
  GND_2: Part2.GND, M3.pin2, M4.pin2, M5.pin2, M6.pin2, J1.gnd

custom parts:
  H-Bridge with L298N: h-bridge
